# Fritzing sketch schematic (saved by Fritzing 0.9.9b)
breadboards: 1

parts:
  Part1 = Arduino Uno (Rev3)
  Passive_Buzzer = Piezo Speaker
  Rotary_Encoder_Module = POT_SWITCH [package=pot_pth_switch]
  MAX7219_LED_Module = LED Matrix - Serial Interface - Red/Green/Blue

nets:
  N1: Part1.D8, Passive_Buzzer.pin2
  N2: Part1.D10_PWM/SS, MAX7219_LED_Module.CLK
  N3: Part1.D11_PWM/MOSI, MAX7219_LED_Module.CS
  N4: Part1.D12/MISO, MAX7219_LED_Module.DIN
  GND: Part1.GND, Passive_Buzzer.pin1, Rotary_Encoder_Module.GND, MAX7219_LED_Module.GND
  N5: Part1.D2, Rotary_Encoder_Module.CLK
  N6: Part1.D3_PWM, Rotary_Encoder_Module.DT
  N7: Part1.D4, Rotary_Encoder_Module.SW
  5V: Part1.5V, Rotary_Encoder_Module.+, MAX7219_LED_Module.VCC

notes:
  +
  GND
  CLK
  DT
  SW
  CS
  DIN
  VCC

custom parts:
  POT_SWITCH: Potentiometer w/ switch.
  LED Matrix - Serial Interface - Red/Green/Blue: Description: This is a large sized RGB LED Matrix with a backpack that has been designed to take SPI serial input and display any graphics you pass it. All the refreshing and communication control is taken care of by the backpack. It's even reprogrammable! 7 software selectable colors are available! Unit comes with a Red/Green/Blue LED Matrix assembled with a RGB Matrix Backpack Controller.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
